// Logisim project alu.circ as structural Verilog: 2 circuits, main circuit alu
module alu (
  input  [31:0] A,
  input  [31:0] B,
  input  [3:0] ALUSel,
  output [31:0] Result
);

  wire slt7;
  wire [31:0] add0, and1, divu8, mul10, mulhu11, multiplier_1_out, or2, remu9, sll6, sra5, srl4, sub13, xor3;

  Adder #(.width(32)) adder_1 (.a(A), .b(B), .out(add0));  // open: cin, cout
  assign and1 = A & B;  // AND_Gate and_1, 32 bits wide
  assign or2 = A | B;  // OR_Gate or_1, 32 bits wide
  assign xor3 = A ^ B;  // XOR_Gate xor_1, 32 bits wide
  Shifter #(.width(32), .shift("lr")) shifter_1 (.in(A), .\dist (B[4:0]), .out(srl4));
  Shifter #(.width(32), .shift("ar")) shifter_2 (.in(A), .\dist (B[4:0]), .out(sra5));
  Shifter #(.width(32)) shifter_3 (.in(A), .\dist (B[4:0]), .out(sll6));
  Comparator #(.width(32)) comparator_1 (.a(A), .b(B), .lt(slt7));  // open: gt, eq
  Multiplier #(.width(32)) multiplier_1 (.a(B), .b(divu8), .out(multiplier_1_out));  // open: cin, cout
  Divider #(.width(32)) divider_1 (.a(A), .b(B), .out(divu8));  // open: upper, rem
  Subtractor #(.width(32)) subtractor_1 (.a(A), .b(multiplier_1_out), .out(remu9));  // open: bin, bout
  Multiplier #(.width(32)) multiplier_2 (.a(A), .b(B), .out(mul10), .cout(mulhu11));  // open: cin
  Subtractor #(.width(32)) subtractor_2 (.a(A), .b(B), .out(sub13));  // open: bin, bout

  // Other names for the same wires on the sheet: bsel14[31:0] = B

  // Notes on the sheet:
  //   INPUTS to your circuit
  //   DON'T CHANGE THE LOCATIONS OF THE INPUTS AND OUTPUTS!
  //   OUTPUT from your circuit
endmodule

module test (
  input  [31:0] in_1,
  input  [31:0] in_2,
  output [31:0] out_3,
  output [31:0] out_4
);

  Multiplier #(.width(32)) multiplier_1 (.a(in_1), .b(in_2), .out(out_3), .cout(out_4));  // open: cin
endmodule
